// Digital circuit ALU.dig as structural Verilog
module ALU (
  input  [15:0] D1,
  input  [15:0] D2,
  input  S1,
  input  S2,
  input  S3,
  input  S4,
  input  C_IN,
  input  [5:0] D3,
  input  Latch,
  output [15:0] Q,
  output C_OUT,
  output gt,
  output eq,
  output lt,
  output Z_FLAG
);

  wire add_1_c_o, decoder_1_out_1, decoder_1_out_2, decoder_1_out_3, decoder_1_out_4, decoder_1_out_5,
       decoder_1_out_6, decoder_1_out_7, decoder_1_out_8, decoder_1_out_9, sub_1_c_o;
  wire [5:0] d_ff_3_q;
  wire [15:0] add_1_s, and_2_out, d_ff_1_q, d_ff_2_q, nand_1_out, not_1_out, or_1_out, sub_1_s, undriven,
       undriven_2, xor_1_out, xor_2_out;

  D_FF #(.Bits(16)) d_ff_1 (.D(D1), .C(Latch), .Q(d_ff_1_q));  // open: nQ
  D_FF #(.Bits(16)) d_ff_2 (.D(D2), .C(Latch), .Q(d_ff_2_q));  // open: nQ
  D_FF #(.Bits(6)) d_ff_3 (.D(D3), .C(Latch), .Q(d_ff_3_q));  // open: nQ
  assign xor_1_out = D1 ^ {16{1'b0}};  // XOr xor_1, 16 bits wide
  Decoder #(.Selector_Bits(4)) decoder_1 (
    .sel({S4, S3, S2, S1}), .out_1(decoder_1_out_1), .out_2(decoder_1_out_2), .out_3(decoder_1_out_3),
    .out_4(decoder_1_out_4), .out_5(decoder_1_out_5), .out_6(decoder_1_out_6), .out_7(decoder_1_out_7),
    .out_8(decoder_1_out_8), .out_9(decoder_1_out_9));  // open: out_0, out_10, out_11, out_12, out_13, out_14, out_15
  and and_1 (Z_FLAG, xor_1_out[0], xor_1_out[1], xor_1_out[2], xor_1_out[3], xor_1_out[4], xor_1_out[5], xor_1_out[6], xor_1_out[7], xor_1_out[8], xor_1_out[9], xor_1_out[10], xor_1_out[11], xor_1_out[12], xor_1_out[13], xor_1_out[14], xor_1_out[15]);
  Add #(.Bits(16)) add_1 (.a(d_ff_1_q), .b(d_ff_2_q), .c_i(C_IN), .s(add_1_s), .c_o(add_1_c_o));
  Sub #(.Bits(16)) sub_1 (.a(d_ff_1_q), .b(d_ff_2_q), .c_i(C_IN), .s(sub_1_s), .c_o(sub_1_c_o));
  assign and_2_out = d_ff_1_q & d_ff_2_q;  // And and_2, 16 bits wide
  assign or_1_out = d_ff_1_q | d_ff_2_q;  // Or or_1, 16 bits wide
  assign nand_1_out = ~(d_ff_1_q & d_ff_2_q);  // NAnd nand_1, 16 bits wide
  assign not_1_out = ~d_ff_1_q;  // Not not_1, 16 bits wide
  BarrelShifter #(.barrelShifterMode("arithmetic"), .Bits(16), .barrelSigned("true")) barrelshifter_1 (
    .in(d_ff_1_q), .shift(d_ff_3_q));  // open: out
  BarrelShifter #(.barrelShifterMode("arithmetic"), .Bits(16), .barrelSigned("true"), .direction("right")) barrelshifter_2 (
    .in(d_ff_1_q), .shift(d_ff_3_q));  // open: out
  assign xor_2_out = d_ff_1_q ^ d_ff_2_q;  // XOr xor_2, 16 bits wide
  Comparator #(.Bits(16)) comparator_1 (.a(d_ff_1_q), .b(d_ff_2_q), .gt(gt), .eq(eq), .lt(lt));
  assign Q = decoder_1_out_1 ? add_1_s : 16'bz;  // Driver driver_1
  assign Q = decoder_1_out_2 ? sub_1_s : 16'bz;  // Driver driver_2
  assign Q = decoder_1_out_3 ? and_2_out : 16'bz;  // Driver driver_3
  assign Q = decoder_1_out_4 ? or_1_out : 16'bz;  // Driver driver_4
  assign Q = decoder_1_out_5 ? nand_1_out : 16'bz;  // Driver driver_5
  assign Q = decoder_1_out_6 ? not_1_out : 16'bz;  // Driver driver_6
  assign Q = decoder_1_out_7 ? undriven : 16'bz;  // Driver driver_7
  assign Q = decoder_1_out_8 ? undriven_2 : 16'bz;  // Driver driver_8
  Driver #(.Bits(16)) driver_9 (.in(xor_2_out), .en(decoder_1_out_9));  // open: out
  PullDown #(.Bits(16)) pulldown_1 (.out(Q));
  assign C_OUT = decoder_1_out_2 ? sub_1_c_o : 1'bz;  // Driver driver_10
  assign C_OUT = decoder_1_out_1 ? add_1_c_o : 1'bz;  // Driver driver_11
  PullDown pulldown_2 (.out(C_OUT));
endmodule
