// Digital circuit CPU-V2.dig as structural Verilog
module CPU_V2 (
  input  CLK
);

  wire _2_WORD_INSTR, and_1_out, and_2_out, decoder_1_out_0, decoder_1_out_1, decoder_1_out_2,
       decoder_1_out_3, decoder_1_out_4, decoder_1_out_5, decoder_1_out_6, decoder_1_out_7, decoder_2_out_0,
       decoder_2_out_1, decoder_2_out_2, decoder_2_out_3, decoder_2_out_4, decoder_2_out_5, decoder_2_out_6,
       decoder_2_out_7, delay_2_out, delay_3_out, delay_4_out, delay_5_out, delay_6_out, delay_7_out,
       delay_8_out, INSTR_DATA, INSTR_REG, LD_Data, LD_INSTR, REG_LD, REG_OUT;
  wire [1:0] bitselector_1_out, counter_1_out;
  wire [3:0] driver_2_out, driver_3_out;
  wire [7:2] rom_2_d;
  wire [9:0] d_ff_1_q, d_ff_2_q;
  wire [15:0] B_q, C_q, counterpreset_1_out, D_q, delay_1_out, driver_1_out, E_q, eeprom_1_d, F_q, G_q, I_q,
       register_1_q, register_2_q, register_3_q, register_4_q, register_5_q, register_6_q, register_7_q,
       register_8_q, register_9_q;
  wire [23:5] rom_1_d;

  CounterPreset #(.Bits(16)) counterpreset_1 (
    .en(1'b1), .C(CLK), .dir(1'b0), .in({16{1'b0}}), .ld(1'b0), .clr(1'b0), .out(counterpreset_1_out));  // open: ovf
  Delay #(.Bits(16), .delayTime(10)) delay_1 (.in(counterpreset_1_out), .out(delay_1_out));
  EEPROM #(.AddrBits(16), .Bits(16)) eeprom_1 (.A(delay_1_out), .CS(1'b1), .WE(1'b0), .OE(1'b1), .D(eeprom_1_d));
  Delay delay_2 (.in(delay_3_out), .out(delay_2_out));
  Register #(.Bits(16)) register_1 (.D(eeprom_1_d), .C(delay_2_out), .en(1'b1), .Q(register_1_q));
  Register #(.Bits(16)) register_2 (.D(register_1_q), .C(delay_3_out), .en(1'b1), .Q(register_2_q));
  Delay delay_3 (.in(delay_4_out), .out(delay_3_out));
  // Probe on register_1_q
  Register #(.Bits(16)) register_3 (.D(register_2_q), .C(delay_4_out), .en(1'b1), .Q(register_3_q));
  // Probe on register_2_q
  Delay delay_4 (.in(delay_5_out), .out(delay_4_out));
  Register #(.Bits(16)) register_4 (.D(register_3_q), .C(delay_5_out), .en(1'b1), .Q(register_4_q));
  Delay delay_5 (.in(delay_6_out), .out(delay_5_out));
  // Probe on register_3_q
  Register #(.Bits(16)) register_5 (.D(register_4_q), .C(delay_6_out), .en(1'b1), .Q(register_5_q));
  // Probe on register_4_q
  Delay delay_6 (.in(delay_7_out), .out(delay_6_out));
  Register #(.Bits(16)) register_6 (.D(register_5_q), .C(delay_7_out), .en(1'b1), .Q(register_6_q));
  Delay delay_7 (.in(CLK), .out(delay_7_out));
  // Probe on register_5_q
  Register #(.Bits(16)) register_7 (.D(register_6_q), .C(CLK), .en(1'b1), .Q(register_7_q));
  // Probe on register_6_q
  and and_1 (and_1_out, CLK, _2_WORD_INSTR);
  // Probe on register_7_q
  Register #(.Bits(16)) register_8 (.D(register_7_q), .C(LD_INSTR), .en(CLK), .Q(register_8_q));
  Register #(.Bits(16)) register_9 (.D(register_7_q), .C(LD_Data), .en(CLK), .Q(register_9_q));
  Counter #(.Bits(2)) counter_1 (.en(1'b1), .C(and_1_out), .clr(and_2_out), .out(counter_1_out));  // open: ovf
  ROM #(.AddrBits(16), .Bits(24)) rom_1 (
    .A(register_8_q), .sel(1'b1), .D({rom_1_d, INSTR_DATA, INSTR_REG, REG_OUT, REG_LD, _2_WORD_INSTR}));
  BitSelector bitselector_1 (.in({counter_1_out[0], CLK}), .sel(_2_WORD_INSTR), .out(bitselector_1_out[0]));
  and and_2 (and_2_out, counter_1_out[0], counter_1_out[1]);
  assign driver_1_out = INSTR_REG ? register_9_q : 16'bz;  // Driver driver_1
  and and_3 (bitselector_1_out[1], counter_1_out[1], _2_WORD_INSTR);
  ROM #(.AddrBits(4), .Bits(8)) rom_2 (
    .A({1'b0, INSTR_DATA, bitselector_1_out}), .sel(1'b1), .D({rom_2_d, LD_Data, LD_INSTR}));
  Delay delay_8 (.in(CLK), .out(delay_8_out));
  D_FF #(.Bits(10)) d_ff_1 (.D({driver_1_out[7:0], REG_OUT, REG_LD}), .C(delay_8_out), .Q(d_ff_1_q));  // open: nQ
  D_FF #(.Bits(10)) d_ff_2 (.D(d_ff_1_q), .C(CLK), .Q(d_ff_2_q));  // open: nQ
  assign driver_2_out = d_ff_2_q[0] ? d_ff_2_q[5:2] : 4'bz;  // Driver driver_2
  assign driver_2_out = ~d_ff_2_q[0] ? 4'b1111 : 4'bz;  // DriverInvSel driverinvsel_1
  assign driver_3_out = d_ff_2_q[1] ? d_ff_2_q[9:6] : 4'bz;  // Driver driver_3
  assign driver_3_out = ~d_ff_2_q[1] ? 4'b1111 : 4'bz;  // DriverInvSel driverinvsel_2
  Decoder #(.Selector_Bits(4)) decoder_1 (
    .sel(driver_2_out), .out_0(decoder_1_out_0), .out_1(decoder_1_out_1), .out_2(decoder_1_out_2),
    .out_3(decoder_1_out_3), .out_4(decoder_1_out_4), .out_5(decoder_1_out_5), .out_6(decoder_1_out_6),
    .out_7(decoder_1_out_7));  // open: out_8, out_9, out_10, out_11, out_12, out_13, out_14, out_15
  Decoder #(.Selector_Bits(4)) decoder_2 (
    .sel(driver_3_out), .out_0(decoder_2_out_0), .out_1(decoder_2_out_1), .out_2(decoder_2_out_2),
    .out_3(decoder_2_out_3), .out_4(decoder_2_out_4), .out_5(decoder_2_out_5), .out_6(decoder_2_out_6),
    .out_7(decoder_2_out_7));  // open: out_8, out_9, out_10, out_11, out_12, out_13, out_14, out_15
  // Probe on driver_2_out
  Register #(.Bits(16)) B (.D(driver_1_out), .C(decoder_1_out_1), .en(1'b1), .Q(B_q));
  assign driver_1_out = decoder_2_out_1 ? B_q : 16'bz;  // Driver driver_4
  Register #(.Bits(16)) C (.D(driver_1_out), .C(decoder_1_out_2), .en(1'b1), .Q(C_q));
  assign driver_1_out = decoder_2_out_2 ? C_q : 16'bz;  // Driver driver_5
  Register #(.Bits(16)) D (.D(driver_1_out), .C(decoder_1_out_3), .en(1'b1), .Q(D_q));
  assign driver_1_out = decoder_2_out_3 ? D_q : 16'bz;  // Driver driver_6
  Register #(.Bits(16)) E (.D(driver_1_out), .C(decoder_1_out_4), .en(1'b1), .Q(E_q));
  assign driver_1_out = decoder_2_out_4 ? E_q : 16'bz;  // Driver driver_7
  Register #(.Bits(16)) F (.D(driver_1_out), .C(decoder_1_out_5), .en(1'b1), .Q(F_q));
  assign driver_1_out = decoder_2_out_5 ? F_q : 16'bz;  // Driver driver_8
  Register #(.Bits(16)) G (.D(driver_1_out), .C(decoder_1_out_6), .en(1'b1), .Q(G_q));
  assign driver_1_out = decoder_2_out_6 ? G_q : 16'bz;  // Driver driver_9
  Register #(.Bits(16)) I (.D(driver_1_out), .C(decoder_1_out_7), .en(1'b1), .Q(I_q));
  assign driver_1_out = decoder_2_out_7 ? I_q : 16'bz;  // Driver driver_10

  // Notes on the sheet:
  //   PC
  //   PROGRAM ROM
  //   contents of eeprom_1 (hex, n*v repeats v):
  //   1,2
  //   INSTR DECODER
  //   contents of rom_1 (hex, n*v repeats v):
  //   0,1b,15*0,1000,17*0,12,524*0,18,2003
  //   contents of rom_2 (hex, n*v repeats v):
  //   0,1,2,0,0,3,2,10*0,1000,17*0,12,524*0,18,2003
endmodule
